# Fritzing sketch toilet-light-rotating-sign (saved by Fritzing 0.9.3b)
breadboards: 1

parts:
  R1 = Photocell (LDR) [package=THT]
  MOTOR1 = 28BYJ-48 Stepper Motor
  BREAKOUT1 = ULN2003A breakout board
  Part1 = Arduino Pro Mini v13
  LED2 = smd LED [color="Red (633nm)" package="0805 [SMD]"]  # not connected
  LED3 = smd LED [color="Red (633nm)" package="0805 [SMD]"]
  LED4 = smd LED [color="Red (633nm)" package="0805 [SMD]"]
  LED5 = smd LED [color="Red (633nm)" package="0805 [SMD]"]
  LED6 = smd LED [color="Red (633nm)" package="0805 [SMD]"]
  LED7 = smd LED [color="Red (633nm)" package="0805 [SMD]"]
  U1 = RELAY [package=relay-jzc]
  R2 = Resistor [tolerance=±5% resistance=10k package=THT]

nets:
  N1: R1.pin_0, BREAKOUT1.0V, Part1.GND, LED3.cathode, LED4.cathode, LED5.cathode, LED6.cathode, LED7.cathode, U1.COIL1
  N2: R1.pin_1, Part1.A3, R2.Pin_0
  N3: MOTOR1.RED, BREAKOUT1.RED_wire
  N4: MOTOR1.ORANGE, BREAKOUT1.ORANGE_wire
  N5: MOTOR1.YELLOW, BREAKOUT1.YELLOW_wire
  N6: MOTOR1.PINK, BREAKOUT1.PINK_wire
  N7: MOTOR1.BLUE, BREAKOUT1.BLUE_wire
  N8: BREAKOUT1.In_1, Part1.D6_PWM
  N9: BREAKOUT1.In_2, Part1.D5_PWM
  N10: BREAKOUT1.In_3, Part1.D4
  N11: BREAKOUT1.In_4, Part1.D3_PWM
  +5V: BREAKOUT1.+5V, Part1.VCC, U1.COIL2, R2.Pin_1
  N12: Part1.D10_PWM/SS, U1.MAIN
  N13: LED3.anode, LED4.anode, LED5.anode, LED6.anode, LED7.anode, U1.NO

custom parts:
  ULN2003A breakout board: ULN2003A 7-way Darlington Transistor Driver on breakoutboard
